// Logisim project Assingment4Final (1).circ as structural Verilog: 3 circuits, main circuit main
module main (
  input  [1:0] in_1,
  input  OP,
  input  [1:0] _00_A_01_B_10_C,
  input  [1:0] in_4,
  input  [7:0] USER_INPUT,
  input  [3:0] USER_INPUT_2,
  input  [3:0] USER_INPUT_3,
  output [7:0] OUTPut,
  output step_counter,
  output [3:0] out_10,
  output [3:0] out_11
);

  wire _0_2_out, _0_3_out, _0_4_out, _0_5_out, _0_6_out, _0_7_out, _0_8_out, _0_9_out, _0_out, _1_2_out,
       _1_3_out, _1_4_out, _1_5_out, _1_6_out, _1_7_out, _1_8_out, _1_9_out, _1_out, _2_2_out, _2_3_out,
       _2_4_out, _2_5_out, _2_6_out, _2_7_out, _2_8_out, _2_9_out, _2_out, _3_2_out, _3_3_out, _3_4_out,
       _3_5_out, _3_6_out, _3_7_out, _3_8_out, _3_9_out, _3_out, _4_2_out, _4_3_out, _4_out, _5_2_out,
       _5_3_out, _5_out, _6_2_out, _6_3_out, _6_out, _7_2_out, _7_3_out, _7_out, and_1_out, and_2_out,
       and_3_out, and_4_out, clock_1_out, control_unit_out_4, control_unit_out_5,
       Merge_only_works_if_R1_is_A_out, not_1_out, OP_q, or_1_out, or_3_out, or_5_out, or_14_out, or_16_out,
       or_22_out, or_23_out;
  wire [1:0] R1_q, R2_q, R3_q;
  wire [3:0] or_17_out, or_19_out;
  wire [7:0] or_21_out;

  Register #(.width(1)) u_OP (.D(OP), .Q(OP_q), .clk(clock_1_out));  // open: en, clr
  Clock clock_1 (.out(clock_1_out));
  Register #(.width(2)) R1 (.D(_00_A_01_B_10_C), .Q(R1_q), .clk(clock_1_out));  // open: en, clr
  Register #(.width(2)) R2 (.D(in_1), .Q(R2_q), .clk(clock_1_out));  // open: en, clr
  cu control_unit (
    .op_code(OP_q), .in_2(clock_1_out), .step_counter(step_counter), .out_4(control_unit_out_4),
    .out_5(control_unit_out_5));
  Register #(.width(2)) R3 (.D(in_4), .Q(R3_q), .clk(clock_1_out));  // open: en, clr
  or or_1 (or_1_out, control_unit_out_5, control_unit_out_4);
  and Merge_only_works_if_R1_is_A (Merge_only_works_if_R1_is_A_out, ~R1_q[0], ~R1_q[1], control_unit_out_5);  // AND_Gate
  and _0 (_0_out, or_1_out, ~R1_q[0], ~R1_q[1], _0_9_out);  // AND_Gate
  and _1 (_1_out, or_1_out, ~R1_q[0], ~R1_q[1], _1_9_out);  // AND_Gate
  and _2 (_2_out, or_1_out, ~R1_q[0], ~R1_q[1], _2_8_out);  // AND_Gate
  and _3 (_3_out, or_1_out, ~R1_q[0], ~R1_q[1], _3_9_out);  // AND_Gate
  and _4 (_4_out, ~R1_q[0], ~R1_q[1], or_1_out, _4_3_out);  // AND_Gate
  and _5 (_5_out, ~R1_q[0], ~R1_q[1], or_1_out, _5_3_out);  // AND_Gate
  and _6 (_6_out, ~R1_q[0], ~R1_q[1], or_1_out, _6_3_out);  // AND_Gate
  and _7 (_7_out, ~R1_q[0], ~R1_q[1], or_1_out, _7_3_out);  // AND_Gate
  and _0_2 (_0_2_out, or_1_out, R1_q[0], ~R1_q[1], _0_9_out);  // AND_Gate
  and _1_2 (_1_2_out, or_1_out, R1_q[0], ~R1_q[1], _1_9_out);  // AND_Gate
  and _2_2 (_2_2_out, or_1_out, R1_q[0], ~R1_q[1], _2_8_out);  // AND_Gate
  and _3_2 (_3_2_out, or_1_out, R1_q[0], ~R1_q[1], _3_9_out);  // AND_Gate
  and _0_3 (_0_3_out, or_1_out, ~R1_q[0], R1_q[1], _0_9_out);  // AND_Gate
  and _1_3 (_1_3_out, or_1_out, ~R1_q[0], R1_q[1], _1_9_out);  // AND_Gate
  and _2_3 (_2_3_out, or_1_out, ~R1_q[0], R1_q[1], _2_8_out);  // AND_Gate
  and _3_3 (_3_3_out, or_1_out, ~R1_q[0], R1_q[1], _3_9_out);  // AND_Gate
  or or_2 (or_21_out[4], or_3_out, USER_INPUT[4]);
  buf or_3 (or_3_out, _4_out);  // OR_Gate
  or or_4 (or_21_out[5], or_5_out, USER_INPUT[5]);
  buf or_5 (or_5_out, _5_out);  // OR_Gate
  or or_6 (or_17_out[2], USER_INPUT_2[2], _2_2_out);
  or or_7 (or_17_out[3], USER_INPUT_2[3], _3_2_out);
  or or_8 (or_19_out[2], USER_INPUT_3[2], _2_3_out);
  or or_9 (or_19_out[3], USER_INPUT_3[3], _3_3_out);
  or or_10 (or_21_out[1], USER_INPUT[1], _1_out);
  or or_11 (or_21_out[2], USER_INPUT[2], _2_out);
  or or_12 (or_21_out[3], USER_INPUT[3], _3_out);
  or or_13 (or_21_out[6], or_14_out, USER_INPUT[6]);
  buf or_14 (or_14_out, _6_out);  // OR_Gate
  or or_15 (or_21_out[7], or_16_out, USER_INPUT[7]);
  buf or_16 (or_16_out, _7_out);  // OR_Gate
  or or_17 (or_17_out[0], _0_2_out, USER_INPUT_2[0]);
  or or_18 (or_17_out[1], _1_2_out, USER_INPUT_2[1]);
  or or_19 (or_19_out[0], _0_3_out, USER_INPUT_3[0]);
  or or_20 (or_19_out[1], _1_3_out, USER_INPUT_3[1]);
  or or_21 (or_21_out[0], USER_INPUT[0], _0_out);
  Register A (.D(or_21_out), .Q(OUTPut), .clk(clock_1_out));  // open: en, clr
  Register #(.width(4)) B (.D(or_17_out), .Q(out_10), .clk(clock_1_out));  // open: en, clr
  Register #(.width(4)) C (.D(or_19_out), .Q(out_11), .clk(clock_1_out));  // open: en, clr
  and _7_2 (_7_2_out, OUTPut[7], or_1_out, ~R1_q[1], ~R1_q[0]);  // AND_Gate
  and _3_4 (_3_4_out, out_10[3], or_1_out, ~R2_q[1], R2_q[0], Merge_only_works_if_R1_is_A_out);  // AND_Gate
  and _3_5 (_3_5_out, out_11[3], or_1_out, R2_q[1], ~R2_q[0], Merge_only_works_if_R1_is_A_out);  // AND_Gate
  or _7_3 (_7_3_out, _3_5_out, _3_4_out);
  and _6_2 (_6_2_out, OUTPut[6], or_1_out, ~R1_q[1], ~R1_q[0]);  // AND_Gate
  and _2_4 (_2_4_out, out_10[2], or_1_out, ~R2_q[1], Merge_only_works_if_R1_is_A_out, R2_q[0]);  // AND_Gate
  and _2_5 (_2_5_out, out_11[2], or_1_out, R2_q[1], ~R2_q[0], Merge_only_works_if_R1_is_A_out);  // AND_Gate
  or _6_3 (_6_3_out, _2_5_out, _2_4_out);
  and _5_2 (_5_2_out, OUTPut[5], or_1_out, ~R1_q[1], ~R1_q[0]);  // AND_Gate
  and _4_2 (_4_2_out, OUTPut[4], or_1_out, ~R1_q[1], ~R1_q[0]);  // AND_Gate
  and _1_4 (_1_4_out, out_10[1], or_1_out, ~R2_q[1], Merge_only_works_if_R1_is_A_out, R2_q[0]);  // AND_Gate
  and _1_5 (_1_5_out, out_11[1], or_1_out, R2_q[1], ~R2_q[0], Merge_only_works_if_R1_is_A_out);  // AND_Gate
  or _5_3 (_5_3_out, _1_5_out, _1_4_out);
  and and_1 (and_1_out, R2_q[0], not_1_out);
  and and_2 (and_2_out, R2_q[1], not_1_out);
  and _0_4 (_0_4_out, out_10[0], or_1_out, ~R2_q[1], Merge_only_works_if_R1_is_A_out, R2_q[0]);  // AND_Gate
  and _0_5 (_0_5_out, out_11[0], or_1_out, R2_q[1], ~R2_q[0], Merge_only_works_if_R1_is_A_out);  // AND_Gate
  or _4_3 (_4_3_out, _0_5_out, _0_4_out);
  not not_1 (not_1_out, Merge_only_works_if_R1_is_A_out);
  and _3_6 (_3_6_out, out_11[3], or_1_out, or_22_out, ~or_23_out);  // AND_Gate
  or or_22 (or_22_out, and_2_out, and_3_out);
  and _3_7 (_3_7_out, OUTPut[3], or_1_out, ~or_22_out, ~or_23_out);  // AND_Gate
  and _3_8 (_3_8_out, out_10[3], or_1_out, ~or_22_out, or_23_out);  // AND_Gate
  or _3_9 (_3_9_out, _3_6_out, _3_8_out, _3_7_out);
  and and_3 (and_3_out, R3_q[1], Merge_only_works_if_R1_is_A_out);
  and and_4 (and_4_out, R3_q[0], Merge_only_works_if_R1_is_A_out);
  or or_23 (or_23_out, and_1_out, and_4_out);
  and _2_6 (_2_6_out, out_10[2], or_1_out, ~or_22_out, or_23_out);  // AND_Gate
  and _2_7 (_2_7_out, out_11[2], or_1_out, or_22_out, ~or_23_out);  // AND_Gate
  or _2_8 (_2_8_out, _2_7_out, _2_6_out, _2_9_out);
  and _2_9 (_2_9_out, OUTPut[2], or_1_out, ~or_22_out, ~or_23_out);  // AND_Gate
  and _1_6 (_1_6_out, out_11[1], or_1_out, or_22_out, ~or_23_out);  // AND_Gate
  and _1_7 (_1_7_out, OUTPut[1], or_1_out, ~or_22_out, ~or_23_out);  // AND_Gate
  and _1_8 (_1_8_out, out_10[1], or_1_out, ~or_22_out, or_23_out);  // AND_Gate
  and _0_6 (_0_6_out, out_11[0], or_1_out, or_22_out, ~or_23_out);  // AND_Gate
  or _1_9 (_1_9_out, _1_6_out, _1_8_out, _1_7_out);
  and _0_7 (_0_7_out, OUTPut[0], or_1_out, ~or_22_out, ~or_23_out);  // AND_Gate
  and _0_8 (_0_8_out, out_10[0], or_1_out, ~or_22_out, or_23_out);  // AND_Gate
  or _0_9 (_0_9_out, _0_6_out, _0_8_out, _0_7_out);

  // Notes on the sheet:
  //   0=Move/1=Merge
  //   MAKE SURE that the input pins for the REGISTER YOU ARE WRITING TO is set to 0000 or else it will interfere with the read data from other registers
endmodule

module Full_Adder (
  input  Cin,
  input  A,
  input  B,
  output Sum,
  output Cout
);

  wire and_1_out, and_2_out, xor_1_out;

  xor xor_1 (xor_1_out, A, B);
  xor xor_2 (Sum, xor_1_out, Cin);
  and and_1 (and_1_out, Cin, xor_1_out);
  and and_2 (and_2_out, B, A);
  or or_1 (Cout, and_1_out, and_2_out);
endmodule

module cu (
  input  op_code,
  input  in_2,
  output step_counter,
  output out_4,
  output out_5
);

  wire _00_out, _0_out, Adder_cout, Adder_sum, and_1_out, and_2_out, and_3_out, Exit_out, not_1_out;

  not not_1 (not_1_out, op_code);
  buf and_1 (and_1_out, not_1_out);  // AND_Gate AND_Gate
  buf and_2 (and_2_out, op_code);  // AND_Gate
  Register #(.width(1)) Step (.D(Adder_sum), .Q(step_counter), .clk(in_2));  // open: en, clr
  and _0 (_0_out, ~step_counter, and_1_out);  // AND_Gate
  and and_3 (and_3_out, step_counter, and_1_out);
  and _00 (_00_out, ~step_counter, and_2_out);  // AND_Gate
  and Exit (Exit_out, step_counter, and_2_out);
  Full_Adder Adder (.Cin(1'b0), .A(1'b1), .B(step_counter), .Sum(Adder_sum), .Cout(Adder_cout));
  or or_1 (out_5, _00_out, Exit_out);
  or or_2 (out_4, _0_out, and_3_out);
endmodule
