// Logisim project ass2Christopher (1).circ as structural Verilog: 1 circuit, main circuit main
module main (
  input  [3:0] Data,
  input  [1:0] Address,
  input  in_3,
  output [3:0] Output
);

  wire and_1_out, and_2_out, and_3_out, and_4_out, and_5_out, and_6_out, and_7_out, and_8_out, and_9_out,
       and_10_out, and_11_out, and_12_out, and_13_out, and_14_out, and_15_out, and_16_out, and_17_out,
       and_18_out, and_19_out, and_20_out, and_21_out, and_22_out, and_23_out, and_24_out, and_25_out,
       and_26_out, and_27_out, and_28_out, and_29_out, and_30_out, and_31_out, and_32_out, and_33_out,
       and_34_out, and_35_out, and_36_out, clock_1_out, d_ff_1_q, d_ff_2_q, d_ff_3_q, d_ff_4_q, d_ff_5_q,
       d_ff_6_q, d_ff_7_q, d_ff_8_q, d_ff_9_q, d_ff_10_q, d_ff_11_q, d_ff_12_q, d_ff_13_q, d_ff_14_q,
       d_ff_15_q, d_ff_16_q, not_1_out, not_2_out, not_3_out, not_4_out, not_5_out;

  not not_1 (not_1_out, Address[1]);
  not not_2 (not_2_out, Address[0]);
  not not_3 (not_3_out, Address[1]);
  not not_4 (not_4_out, Address[0]);
  and and_1 (and_1_out, Address[1], Address[0], clock_1_out);
  and and_2 (and_2_out, Address[0], not_1_out);
  and and_3 (and_3_out, Address[1], clock_1_out, not_2_out);
  and and_4 (and_4_out, not_3_out, not_3_out, not_4_out, clock_1_out);
  and and_5 (and_5_out, in_3, Data[3], clock_1_out, and_1_out);
  and and_6 (and_6_out, in_3, Data[3], and_2_out, clock_1_out);
  and and_7 (and_7_out, in_3, Data[3], and_3_out, and_3_out, clock_1_out);
  and and_8 (and_8_out, in_3, clock_1_out, and_4_out, Data[3]);
  Clock clock_1 (.out(clock_1_out));
  not not_5 (not_5_out, in_3);
  D_Flip_Flop #(.trigger("falling")) d_ff_1 (
    .clk(clock_1_out), .D(and_5_out), .Q(d_ff_1_q));  // open: Qn, preset, en, reset
  D_Flip_Flop #(.trigger("falling")) d_ff_2 (
    .clk(clock_1_out), .D(and_6_out), .Q(d_ff_2_q));  // open: Qn, preset, en, reset
  D_Flip_Flop #(.trigger("falling")) d_ff_3 (
    .clk(clock_1_out), .D(and_7_out), .Q(d_ff_3_q));  // open: Qn, preset, en, reset
  D_Flip_Flop #(.trigger("falling")) d_ff_4 (
    .clk(clock_1_out), .D(and_8_out), .Q(d_ff_4_q));  // open: Qn, preset, en, reset
  and and_9 (and_9_out, not_5_out, d_ff_1_q, and_1_out);
  and and_10 (and_10_out, not_5_out, d_ff_2_q, and_2_out);
  and and_11 (and_11_out, not_5_out, d_ff_3_q, and_3_out);
  and and_12 (and_12_out, not_5_out, d_ff_4_q, and_4_out, and_4_out);
  and and_13 (and_13_out, in_3, Data[2], clock_1_out, and_1_out);
  and and_14 (and_14_out, in_3, Data[2], clock_1_out, and_2_out);
  and and_15 (and_15_out, in_3, Data[2], clock_1_out, and_3_out);
  and and_16 (and_16_out, in_3, Data[2], clock_1_out, and_4_out);
  D_Flip_Flop #(.trigger("falling")) d_ff_5 (
    .clk(clock_1_out), .D(and_13_out), .Q(d_ff_5_q));  // open: Qn, preset, en, reset
  D_Flip_Flop #(.trigger("falling")) d_ff_6 (
    .clk(clock_1_out), .D(and_14_out), .Q(d_ff_6_q));  // open: Qn, preset, en, reset
  D_Flip_Flop #(.trigger("falling")) d_ff_7 (
    .clk(clock_1_out), .D(and_15_out), .Q(d_ff_7_q));  // open: Qn, preset, en, reset
  D_Flip_Flop #(.trigger("falling")) d_ff_8 (
    .clk(clock_1_out), .D(and_16_out), .Q(d_ff_8_q));  // open: Qn, preset, en, reset
  and and_17 (and_17_out, d_ff_5_q, not_5_out, and_1_out);
  and and_18 (and_18_out, d_ff_6_q, not_5_out, and_2_out);
  and and_19 (and_19_out, not_5_out, d_ff_7_q, and_3_out);
  and and_20 (and_20_out, d_ff_8_q, not_5_out, and_4_out);
  or or_1 (Output[3], and_11_out, and_12_out, and_10_out, and_9_out);
  or or_2 (Output[2], and_17_out, and_20_out, and_19_out, and_18_out);
  and and_21 (and_21_out, Data[1], in_3, and_1_out, clock_1_out);
  D_Flip_Flop #(.trigger("falling")) d_ff_9 (
    .clk(clock_1_out), .D(and_22_out), .Q(d_ff_9_q));  // open: Qn, preset, en, reset
  and and_22 (and_22_out, Data[1], in_3, clock_1_out, and_2_out);
  D_Flip_Flop #(.trigger("falling")) d_ff_10 (
    .clk(clock_1_out), .D(and_23_out), .Q(d_ff_10_q));  // open: Qn, preset, en, reset
  and and_23 (and_23_out, clock_1_out, in_3, Data[1], and_3_out);
  and and_24 (and_24_out, Data[1], in_3, clock_1_out, and_4_out);
  D_Flip_Flop #(.trigger("falling")) d_ff_11 (
    .clk(clock_1_out), .D(and_21_out), .Q(d_ff_11_q));  // open: Qn, preset, en, reset
  and and_25 (and_25_out, not_5_out, d_ff_11_q, and_1_out);
  and and_26 (and_26_out, not_5_out, d_ff_9_q, and_2_out);
  and and_27 (and_27_out, not_5_out, d_ff_10_q, and_3_out);
  D_Flip_Flop #(.trigger("falling")) d_ff_12 (
    .clk(clock_1_out), .D(and_24_out), .Q(d_ff_12_q));  // open: Qn, preset, en, reset
  and and_28 (and_28_out, not_5_out, d_ff_12_q, d_ff_12_q, and_4_out);
  or or_3 (Output[1], and_28_out, and_27_out, and_26_out, and_25_out);
  and and_29 (and_29_out, clock_1_out, in_3, Data[0], in_3, and_1_out);
  and and_30 (and_30_out, clock_1_out, Data[0], in_3, and_2_out, in_3);
  and and_31 (and_31_out, clock_1_out, Data[0], in_3, in_3, and_3_out);
  and and_32 (and_32_out, clock_1_out, Data[0], in_3, in_3, and_4_out);
  D_Flip_Flop #(.trigger("falling")) d_ff_13 (
    .clk(clock_1_out), .D(and_29_out), .Q(d_ff_13_q));  // open: Qn, preset, en, reset
  D_Flip_Flop #(.trigger("falling")) d_ff_14 (
    .clk(clock_1_out), .D(and_30_out), .Q(d_ff_14_q));  // open: Qn, preset, en, reset
  D_Flip_Flop #(.trigger("falling")) d_ff_15 (
    .clk(clock_1_out), .D(and_31_out), .Q(d_ff_15_q));  // open: Qn, preset, en, reset
  D_Flip_Flop #(.trigger("falling")) d_ff_16 (
    .clk(clock_1_out), .D(and_32_out), .Q(d_ff_16_q));  // open: Qn, preset, en, reset
  and and_33 (and_33_out, not_5_out, d_ff_13_q);
  and and_34 (and_34_out, not_5_out, d_ff_14_q);
  and and_35 (and_35_out, d_ff_15_q, not_5_out);
  and and_36 (and_36_out, d_ff_16_q, not_5_out, not_5_out);
  or or_4 (Output[0], and_36_out, and_35_out, and_34_out, and_33_out);

  // Notes on the sheet:
  //   Mode (1=write,0=read)
  //   Clock
  //   DO NOT MOVE the inputs, outputs or clock, Anything else can be moved.
endmodule
