// Logisim project chrisass3 (1).circ as structural Verilog: 4 circuits, main circuit main
module main (
  input  constant_0,
  input  [3:0] L_input,
  input  ALU_input_pin,
  input  [3:0] Rinput,
  output [3:0] A_out,
  output [3:0] status_register
);

  wire _0_2_out, _0_3_out, _0_out, _1_2_out, _1_3_out, _1_out, _2_2_out, _2_3_out, _2_out,
       _2s_Complement_out_5, _2s_Complement_out_6, _2s_Complement_out_7, _2s_Complement_out_8, _3_2_out,
       _3_3_out, _3_out, adder_0_carry, adder_1_carry, not_1_out, not_2_out, not_3_out, not_4_out, not_5_out,
       not_6_out, not_7_out, not_8_out;

  and _0 (_0_out, ALU_input_pin, _2s_Complement_out_5);
  _2s_complement _2s_Complement (
    .in_1(Rinput[0]), .in_2(Rinput[1]), .in_3(Rinput[2]), .in_4(Rinput[3]), .out_5(_2s_Complement_out_5),
    .out_6(_2s_Complement_out_6), .out_7(_2s_Complement_out_7), .out_8(_2s_Complement_out_8));
  not not_1 (not_1_out, ALU_input_pin);
  not not_2 (not_2_out, ALU_input_pin);
  and _1 (_1_out, ALU_input_pin, _2s_Complement_out_6);
  and _2 (_2_out, ALU_input_pin, _2s_Complement_out_7);
  and _3 (_3_out, ALU_input_pin, _2s_Complement_out_8);
  not not_3 (not_3_out, ALU_input_pin);
  and _2_2 (_2_2_out, not_1_out, Rinput[2]);
  and _3_2 (_3_2_out, not_2_out, Rinput[3]);
  and _0_2 (_0_2_out, not_3_out, Rinput[0]);
  not not_4 (not_4_out, ALU_input_pin);
  and _1_2 (_1_2_out, not_4_out, Rinput[1]);
  or _0_3 (_0_3_out, _0_out, _0_2_out);
  or _1_3 (_1_3_out, _1_out, _1_2_out);
  or _2_3 (_2_3_out, _2_out, _2_2_out);
  or _3_3 (_3_3_out, _3_out, _3_2_out);
  rippleader adder_0 (.Cin(constant_0), .A(L_input[0]), .B(_0_3_out), .sum(A_out[0]), .carry(adder_0_carry));
  rippleader adder_1 (.Cin(adder_0_carry), .A(L_input[1]), .B(_1_3_out), .sum(A_out[1]), .carry(adder_1_carry));
  rippleader adder_2 (.Cin(adder_1_carry), .A(L_input[2]), .B(_2_3_out), .sum(A_out[2]), .carry(status_register[1]));
  rippleader adder_3 (
    .Cin(status_register[1]), .A(L_input[3]), .B(_3_3_out), .sum(A_out[3]), .carry(status_register[0]));
  not not_5 (not_5_out, A_out[2]);
  not not_6 (not_6_out, A_out[3]);
  not not_7 (not_7_out, A_out[1]);
  not not_8 (not_8_out, A_out[0]);
  and Zero_status (status_register[2], not_6_out, not_5_out, not_7_out, not_8_out);

  assign status_register[3] = A_out[3];
endmodule

module _1_2_adder (
  input  a,
  input  B,
  output sum,
  output carry
);

  xor xor_1 (sum, a, B);
  and and_1 (carry, a, B, B);
endmodule

module rippleader (
  input  Cin,
  input  A,
  input  B,
  output sum,
  output carry
);

  wire and_1_out, and_2_out, xor_1_out;

  xor xor_1 (xor_1_out, A, B);
  and and_1 (and_1_out, Cin, xor_1_out);
  and and_2 (and_2_out, B, A);
  xor xor_2 (sum, xor_1_out, Cin);
  or or_1 (carry, and_1_out, and_2_out);
endmodule

module _2s_complement (
  input  in_1,
  input  in_2,
  input  in_3,
  input  in_4,
  output out_5,
  output out_6,
  output out_7,
  output out_8
);

  wire n1_2_adder_1_carry, n1_2_adder_2_carry, n1_2_adder_3_carry, not_1_out, not_2_out, not_3_out, not_4_out;

  not not_1 (not_1_out, in_1);
  not not_2 (not_2_out, in_2);
  not not_3 (not_3_out, in_3);
  not not_4 (not_4_out, in_4);
  _1_2_adder u_1_2_adder_1 (.a(1'b1), .B(not_1_out), .sum(out_5), .carry(n1_2_adder_1_carry));
  _1_2_adder u_1_2_adder_2 (.a(n1_2_adder_1_carry), .B(not_2_out), .sum(out_6), .carry(n1_2_adder_2_carry));
  _1_2_adder u_1_2_adder_3 (.a(n1_2_adder_2_carry), .B(not_3_out), .sum(out_7), .carry(n1_2_adder_3_carry));
  _1_2_adder u_1_2_adder_4 (.a(n1_2_adder_3_carry), .B(not_4_out), .sum(out_8));  // open: carry
endmodule
